# Fritzing sketch olivia-piano-wiring (saved by Fritzing 0.9.3b)
breadboards: 1

parts:
  Part1 = Arduino Uno (Rev3)
  R1 = Rotary Potentiometer (Small) [maximum_resistance=100kΩ package=THT]
  R2 = Rotary Potentiometer (Small) [maximum_resistance=100kΩ package=THT]
  U1 = SLIDER [package=slider]
  BUTTON1 = Arcade Button (blue)
  BUTTON2 = Arcade Button (yellow)
  J1 = Basic Force Sensing Resistor (FSR) [package=THT]
  Q1 = Basic FET P-Channel [package="DPak [SMD]"]
  Q2 = Basic FET P-Channel [package="DPak [SMD]"]
  L1 = Solenoid
  L2 = Solenoid
  L3 = Solenoid
  M1 = DC Motor
  M2 = DC Motor
  J2 = Basic Servo
  R3 = Resistor [tolerance=±5% resistance=10k package="0402 [SMD]"]  # not connected
  Q3 = Basic FET P-Channel [package="DPak [SMD]"]
  Q4 = Basic FET P-Channel [package="DPak [SMD]"]
  Q5 = Basic FET P-Channel [package="DPak [SMD]"]
  R4 = Resistor [tolerance=±5% resistance=50 package="0603 [SMD]"]  # not connected

nets:
  N1: Part1.A0, R1.wiper
  N2: Part1.A1, R2.wiper
  N3: Part1.A2, U1.S
  N4: Part1.A3, J1.pin_1
  N5: Part1.D8, Q1.Gate
  N6: Part1.D9_PWM, J2.pulse
  N7: Part1.D2, BUTTON1.no_name_yet#2
  N8: Part1.D3_PWM, Q5.Gate
  N9: Part1.D4, BUTTON2.no_name_yet#2
  N10: Part1.D5_PWM, Q4.Gate
  N11: Part1.D6_PWM, Q3.Gate
  N12: Part1.D7, Q2.Gate
  N13: Part1.5V, R1.leg2, R2.leg2, J1.pin_0, L1.pin2, L2.pin2, L3.pin2, M1.pin_2, M2.pin_2
  N14: Part1.GND, R1.leg1, R2.leg1, U1.E, BUTTON1.no_name_yet#1, BUTTON2.no_name_yet#1, Q1.source, Q2.source, Q3.source, Q4.source, Q5.source
  N15: Q1.drain, L1.pin1
  N16: Q2.drain, L2.pin1
  N17: L3.pin1, Q3.drain
  N18: M1.pin_1, Q4.drain
  N19: M2.pin_1, Q5.drain

custom parts:
  Arcade Button (blue): Adafruit Arcade Button (blue)
  Arcade Button (yellow): Adafruit Arcade Button (yellow)
